# Fritzing sketch Sound Level Meter (saved by Fritzing 0.9.3b)
breadboards: 1

parts:
  Часть2 = Breakout Board for Electret Microphone
  R1 = Trimmer Potentiometer [maximum_resistance=10kΩ package=THT]
  LCD1 = LCD screen
  J1 = Piezo Speaker
  R2 = Resistor [tolerance=±5% resistance=220 package=THT]
  Часть1 = Arduino Uno (Rev3)

nets:
  N1: Часть2.VCC, Часть1.A3
  GND: Часть2.GND, R1.leg2, LCD1.VSS, LCD1.R/W, LCD1.LED-, J1.pin1, Часть1.GND
  VDD: Часть2.AUD, R1.leg1, LCD1.VDD, LCD1.LED+, Часть1.5V
  N2: R1.wiper, LCD1.V0
  N3: LCD1.RS, Часть1.D7
  N4: LCD1.E, Часть1.D6_PWM
  N5: LCD1.DB4, Часть1.D5_PWM
  N6: LCD1.DB5, Часть1.D4
  N7: LCD1.DB6, Часть1.D3_PWM
  N8: LCD1.DB7, Часть1.D2
  N9: J1.pin2, R2.Pin_1
  N10: R2.Pin_0, Часть1.D9_PWM
